# Fritzing sketch Connection (saved by Fritzing 0.9.3b)

parts:
  U1 = ESP8266 NodeMCU LoLin module
  R1 = Slide Potentiometer [maximum_resistance=100kΩ]
  RS485_module1 = RS485 Module (MAX3485)

nets:
  N1: U1.D0, RS485_module1.RE, RS485_module1.DE
  N2: U1.D2, RS485_module1.DI
  N3: U1.D3, RS485_module1.RO
  3V3: U1.3V3, R1.leg2, RS485_module1.VCC
  GND: U1.GND, R1.leg1, RS485_module1.GND

custom parts:
  ESP8266 NodeMCU LoLin module: ESP8266 based NodeMCU
  RS485 Module (MAX3485): Commercially available RS485 to RS232 TTL Module
