# Fritzing sketch LED_Control_NodeMCU_ESP8266 (saved by Fritzing 0.9.3b)

parts:
  U1 = ESP8266 NodeMCU LoLin module
  U2 = WS2812 RGB LED matrix 1x8

nets:
  N1: U1.D1, U2.DIN
  3V3: U1.3V3, U2.VCC
  GND: U1.GND, U2.GND

custom parts:
  ESP8266 NodeMCU LoLin module: ESP8266 based NodeMCU
  WS2812 RGB LED matrix 1x8: WS2812 matrix 1x8
